// Digital circuit CPU.dig as structural Verilog
module CPU (
  input  [15:0] value,
  input  [1:0] dest,
  input  [1:0] src,
  output [15:0] r0,
  output [15:0] r1,
  output [15:0] r2,
  output [15:0] r3,
  output [15:0] B,
  output [1:0] rd,
  output [15:0] A,
  output [1:0] rs,
  output [3:0] out_12,
  output [15:0] A_2
);

  wire add, add_out, assembler_1_store, button_1_out, jump, jump_out, mode_out;
  wire [15:0] execute_1_result;
  wire [31:0] assembler_1_instr, PROGRAM_d;

  LED programming (.in(mode_out));
  DipSwitch mode (.out(mode_out));
  Button u_add (.out(add_out));
  Button u_jump (.out(jump_out));
  assembler assembler_1 (
    .mode(mode_out), .value(value), .dest(dest), .src(src), .add(add_out), .jump(jump_out),
    .instr(assembler_1_instr), .store(assembler_1_store));
  Button button_1 (.out(button_1_out));
  CounterPreset #(.Bits(4), .isProgramCounter("true")) PC (
    .en(1'b1), .C(button_1_out), .dir(1'b0), .in(A[3:0]), .ld(jump), .clr(1'b0), .out(out_12));  // open: ovf
  EEPROMDualPort #(.AddrBits(4), .Bits(32)) PROGRAM (
    .A(out_12), .Din(assembler_1_instr), .str(1'b1), .C(assembler_1_store), .ld(1'b1), .D(PROGRAM_d));
  // decoder decoder_1: pin names not known; wires that end beside it: mode_out, assembler_1_instr, PROGRAM_d, A, rs, rd, add, jump
  LED led_1 (.in(add));
  LED led_2 (.in(jump));
  execute execute_1 (.value(A), .B(B), .add(add), .result(execute_1_result));
  reg_file reg_file_1 (
    .RS(rs), .rd(rd), .result(execute_1_result), .clock(button_1_out), .rsval(B));  // open: rdval, R0, R1, R2, R3

  assign A_2 = A;

  // Notes on the sheet:
  //   value: default 1
  //   dest: default 1
  //   src: default 1
  //   contents of PROGRAM (hex, n*v repeats v):
  //   64,1000c8,1200c8,230022,30002a,7000002
  //   R
  //   pc =
  //   =
  //   +
  //   (
  //   )
endmodule
